// Logisim project XOR.circ as structural Verilog: 1 circuit, main circuit main
module main (
  input  in_1,
  input  in_2,
  output out_3
);

  wire and_1_out, not_1_out, not_2_out, XOR_circuit_out;

  not not_1 (not_1_out, in_1);
  not not_2 (not_2_out, in_2);
  and and_1 (and_1_out, not_1_out, in_2);
  and XOR_circuit (XOR_circuit_out, in_1, not_2_out);
  or or_1 (out_3, and_1_out, XOR_circuit_out);

  // Notes on the sheet:
  //   Tuan Nguyen
  //   January 9.2009
endmodule
