// Logisim project part2.circ as structural Verilog: 1 circuit, main circuit main
module main (
  input  [2:0] in_1,
  output out_2
);

  wire and_1_out;

  and and_1 (and_1_out, in_1[0], in_1[1]);
  or or_1 (out_2, and_1_out, in_1[2]);

  // Other names for the same wires on the sheet: umbrella = out_2

  // Notes on the sheet:
  //   Cloudy
  //   Windy
  //   Service
  //   Tuan Nguyen (tnguyen306: 902779009) 
endmodule
