// Logisim project hw3.circ as structural Verilog: 5 circuits, main circuit 4-bit ALU
module _1_bit_adder (
  input  A,
  input  B,
  input  Cin,
  output out_4,
  output out_5
);

  wire and_1_out, and_2_out, and_3_out, and_4_out, and_5_out, and_6_out, and_7_out;

  and and_1 (and_1_out, ~A, ~B, Cin);  // AND_Gate
  and and_2 (and_2_out, ~A, B, ~Cin);  // AND_Gate
  or or_1 (out_5, and_1_out, and_2_out, and_3_out, and_4_out);
  and and_3 (and_3_out, A, ~B, ~Cin);  // AND_Gate
  and and_4 (and_4_out, A, B, Cin);
  and and_5 (and_5_out, ~A, B, Cin);  // AND_Gate
  and and_6 (and_6_out, A, ~B, Cin);  // AND_Gate
  or or_2 (out_4, and_4_out, and_5_out, and_6_out, and_7_out);
  and and_7 (and_7_out, A, B, ~Cin);  // AND_Gate

  // Other names for the same wires on the sheet: Answer = out_5; Cout = out_4
endmodule

module _4_bit_adder (
  input  [3:0] B,
  input  [3:0] A,
  input  Cin,
  output Cout,
  output [3:0] OutPut
);

  wire n1_bit_adder_2_out_4, n1_bit_adder_3_out_4, n1_bit_adder_4_out_4;

  _1_bit_adder u_1_bit_adder_1 (.A(A[3]), .B(B[3]), .Cin(n1_bit_adder_2_out_4), .out_4(Cout), .out_5(OutPut[3]));
  _1_bit_adder u_1_bit_adder_2 (
    .A(A[2]), .B(B[2]), .Cin(n1_bit_adder_3_out_4), .out_4(n1_bit_adder_2_out_4), .out_5(OutPut[2]));
  _1_bit_adder u_1_bit_adder_3 (
    .A(A[1]), .B(B[1]), .Cin(n1_bit_adder_4_out_4), .out_4(n1_bit_adder_3_out_4), .out_5(OutPut[1]));
  _1_bit_adder u_1_bit_adder_4 (.A(A[0]), .B(B[0]), .Cin(Cin), .out_4(n1_bit_adder_4_out_4), .out_5(OutPut[0]));
endmodule

module _4_bit_ALU (
  input  [3:0] A,
  input  [3:0] B,
  input  [2:0] S,
  output [3:0] OutPut
);

  wire [3:0] and_1_out, n4_bit_adder_1_output, n4_bit_adder_2_output, n4_bit_adder_3_output,
       n4_bit_adder_4_output, n4_bit_adder_5_output, n4_bit_adder_6_output, n4_bit_adder_7_output,
       n4_bit_adder_8_output, n4_bit_adder_9_output, not_1_out, not_2_out, not_3_out, or_1_out, xor_1_out;

  assign not_1_out = ~B;  // NOT_Gate not_1, 4 bits wide
  _4_bit_adder u_4_bit_adder_1 (.B(not_1_out), .A(4'b0000), .OutPut(n4_bit_adder_1_output), .Cin(1'b1));  // open: Cout
  _4_bit_adder u_4_bit_adder_2 (
    .B(A), .A(n4_bit_adder_1_output), .OutPut(n4_bit_adder_2_output), .Cin(1'b0));  // open: Cout
  _4_bit_adder u_4_bit_adder_3 (.B(A), .A(B), .OutPut(n4_bit_adder_3_output), .Cin(1'b0));  // open: Cout
  assign not_2_out = ~n4_bit_adder_4_output;  // NOT_Gate not_2, 4 bits wide
  _4_bit_adder u_4_bit_adder_4 (.B(4'b0000), .A(4'b0000), .OutPut(n4_bit_adder_4_output), .Cin(1'b1));  // open: Cout
  _4_bit_adder u_4_bit_adder_5 (.B(A), .A(not_2_out), .OutPut(n4_bit_adder_5_output), .Cin(1'b1));  // open: Cout
  assign not_3_out = ~A;  // NOT_Gate not_3, 4 bits wide
  _4_bit_adder u_4_bit_adder_6 (.B(not_3_out), .A(4'b0000), .OutPut(n4_bit_adder_6_output), .Cin(1'b1));  // open: Cout
  Multiplexer #(.select(3), .width(4), .disabled(0), .enable("false")) multiplexer_1 (
    .in0(n4_bit_adder_3_output), .in1(n4_bit_adder_2_output), .in2(n4_bit_adder_5_output),
    .in3(n4_bit_adder_6_output), .in4(n4_bit_adder_8_output), .in5(and_1_out), .in6(or_1_out),
    .in7(xor_1_out), .out(OutPut), .sel(S));
  _4_bit_adder u_4_bit_adder_7 (.B(A), .A(A), .OutPut(n4_bit_adder_7_output), .Cin(1'b0));  // open: Cout
  _4_bit_adder u_4_bit_adder_8 (
    .B(n4_bit_adder_7_output), .A(n4_bit_adder_9_output), .OutPut(n4_bit_adder_8_output), .Cin(1'b0));  // open: Cout
  _4_bit_adder u_4_bit_adder_9 (.B(A), .A(A), .OutPut(n4_bit_adder_9_output), .Cin(1'b0));  // open: Cout
  assign and_1_out = A & B;  // AND_Gate and_1, 4 bits wide
  assign or_1_out = A | B;  // OR_Gate or_1, 4 bits wide
  assign xor_1_out = A ^ B;  // XOR_Gate xor_1, 4 bits wide

  // Notes on the sheet:
  //   1-bit-lenght
endmodule

module _16_bit_adder (
  input  [15:0] A,
  input  [15:0] B,
  input  Cin,
  output Cout,
  output [15:0] OutPut
);

  wire n4_bit_adder_2_cout, n4_bit_adder_3_cout, n4_bit_adder_4_cout;

  _4_bit_adder u_4_bit_adder_1 (
    .B(A[15:12]), .A(B[15:12]), .Cout(Cout), .OutPut(OutPut[15:12]), .Cin(n4_bit_adder_2_cout));
  _4_bit_adder u_4_bit_adder_2 (
    .B(A[11:8]), .A(B[11:8]), .Cout(n4_bit_adder_2_cout), .OutPut(OutPut[11:8]), .Cin(n4_bit_adder_3_cout));
  _4_bit_adder u_4_bit_adder_3 (
    .B(A[7:4]), .A(B[7:4]), .Cout(n4_bit_adder_3_cout), .OutPut(OutPut[7:4]), .Cin(n4_bit_adder_4_cout));
  _4_bit_adder u_4_bit_adder_4 (.B(A[3:0]), .A(B[3:0]), .Cout(n4_bit_adder_4_cout), .OutPut(OutPut[3:0]), .Cin(Cin));
endmodule

module _16_bit_ALU (
  input  [15:0] A,
  input  [15:0] B,
  input  [2:0] S,
  output [15:0] OutPut
);

  wire [15:0] and_1_out, n16_bit_adder_1_output, n16_bit_adder_2_output, n16_bit_adder_3_output,
       n16_bit_adder_4_output, n16_bit_adder_5_output, n16_bit_adder_6_output, n16_bit_adder_7_output,
       n16_bit_adder_8_output, n16_bit_adder_9_output, not_1_out, not_2_out, not_3_out, or_1_out, xor_1_out;

  assign not_1_out = ~B;  // NOT_Gate not_1, 16 bits wide
  _16_bit_adder u_16_bit_adder_1 (.A(A), .B(B), .OutPut(n16_bit_adder_1_output), .Cin(1'b0));  // open: Cout
  _16_bit_adder u_16_bit_adder_2 (
    .A(not_1_out), .B({16{1'b0}}), .OutPut(n16_bit_adder_2_output), .Cin(1'b1));  // open: Cout
  _16_bit_adder u_16_bit_adder_3 (
    .A(A), .B(n16_bit_adder_2_output), .OutPut(n16_bit_adder_3_output), .Cin(1'b0));  // open: Cout
  _16_bit_adder u_16_bit_adder_4 (
    .A({16{1'b0}}), .B({16{1'b0}}), .OutPut(n16_bit_adder_4_output), .Cin(1'b1));  // open: Cout
  assign not_2_out = ~n16_bit_adder_4_output;  // NOT_Gate not_2, 16 bits wide
  _16_bit_adder u_16_bit_adder_5 (.A(A), .B(not_2_out), .OutPut(n16_bit_adder_5_output), .Cin(1'b1));  // open: Cout
  assign not_3_out = ~A;  // NOT_Gate not_3, 16 bits wide
  _16_bit_adder u_16_bit_adder_6 (
    .A(not_3_out), .B({16{1'b0}}), .OutPut(n16_bit_adder_6_output), .Cin(1'b1));  // open: Cout
  Multiplexer #(.select(3), .width(16), .disabled(0), .enable("false")) multiplexer_1 (
    .in0(n16_bit_adder_1_output), .in1(n16_bit_adder_3_output), .in2(n16_bit_adder_5_output),
    .in3(n16_bit_adder_6_output), .in4(n16_bit_adder_9_output), .in5(and_1_out), .in6(or_1_out),
    .in7(xor_1_out), .out(OutPut), .sel(S));
  _16_bit_adder u_16_bit_adder_7 (.A(A), .B(A), .OutPut(n16_bit_adder_7_output), .Cin(1'b0));  // open: Cout
  _16_bit_adder u_16_bit_adder_8 (.A(A), .B(A), .OutPut(n16_bit_adder_8_output), .Cin(1'b0));  // open: Cout
  _16_bit_adder u_16_bit_adder_9 (
    .A(n16_bit_adder_7_output), .B(n16_bit_adder_8_output), .OutPut(n16_bit_adder_9_output), .Cin(1'b0));  // open: Cout
  assign and_1_out = A & B;  // AND_Gate and_1, 16 bits wide
  assign or_1_out = A | B;  // OR_Gate or_1, 16 bits wide
  assign xor_1_out = A ^ B;  // XOR_Gate xor_1, 16 bits wide

  // Notes on the sheet:
  //   1-bit-length
endmodule
