// Logisim project hw4part1.circ as structural Verilog: 3 circuits, main circuit Register
module Tester (
  input  [7:0] Input,
  input  Enable,
  output [7:0] Output
);

  wire Clock_out, Reset_out;

  Register register_1 (.Data_In(Input), .Data_Out(Output), .Clock(Clock_out), .Reset(Reset_out), .Enable(Enable));
  Clock Clock (.out(Clock_out));
  Button Reset (.out(Reset_out));

  // Notes on the sheet:
  //   You can use this to test your circuit.
endmodule

module Register (
  input  [7:0] Data_In,
  input  Clock,
  input  Reset,
  input  Enable,
  output [7:0] Data_Out
);

  wire not_1_out;

  not not_1 (not_1_out, Clock);
  D_Flip_Flop d_ff_1 (
    .clk(not_1_out), .D(Data_In[0]), .Q(Data_Out[0]), .en(Enable), .reset(Reset));  // open: Qn, preset
  D_Flip_Flop d_ff_2 (
    .clk(not_1_out), .D(Data_In[1]), .Q(Data_Out[1]), .en(Enable), .reset(Reset));  // open: Qn, preset
  D_Flip_Flop d_ff_3 (
    .clk(not_1_out), .D(Data_In[2]), .Q(Data_Out[2]), .en(Enable), .reset(Reset));  // open: Qn, preset
  D_Flip_Flop d_ff_4 (
    .clk(not_1_out), .D(Data_In[3]), .Q(Data_Out[3]), .en(Enable), .reset(Reset));  // open: Qn, preset
  D_Flip_Flop d_ff_5 (
    .clk(not_1_out), .D(Data_In[4]), .Q(Data_Out[4]), .en(Enable), .reset(Reset));  // open: Qn, preset
  D_Flip_Flop d_ff_6 (.D(Data_In[5]), .Q(Data_Out[5]), .en(Enable), .reset(Reset));  // open: clk, Qn, preset
  D_Flip_Flop d_ff_7 (
    .clk(not_1_out), .D(Data_In[6]), .Q(Data_Out[6]), .en(Enable), .reset(Reset));  // open: Qn, preset
  D_Flip_Flop d_ff_8 (
    .clk(not_1_out), .D(Data_In[7]), .Q(Data_Out[7]), .en(Enable), .reset(Reset));  // open: Qn, preset

  // Other names for the same wires on the sheet: CLK = Clock; D[7:0] = Data_In; EN = Enable; Q[7:0] = Data_Out;
  //   RST = Reset

  // Notes on the sheet:
  //   My name is
  //   Alexa Schlein
  //   and this is my pretty 8-bit register!
endmodule

module hu (
);

  wire and_1_out, and_2_out, and_3_out, and_4_out, and_5_out, and_6_out, and_7_out, and_8_out, CLK,
       not_1_out, RST;
  wire [7:0] D, Q;

  and and_1 (and_1_out, D[0], D[7]);
  and and_2 (and_2_out, D[1], D[7]);
  and and_3 (and_3_out, D[2], D[7]);
  and and_4 (and_4_out, D[3], D[7]);
  and and_5 (and_5_out, D[4], D[7]);
  and and_6 (and_6_out, D[5], D[7]);
  and and_7 (and_7_out, D[7], D[7]);
  and and_8 (and_8_out, D[7], D[7]);
  not not_1 (not_1_out, CLK);
  D_Flip_Flop d_ff_1 (.clk(not_1_out), .D(and_1_out), .Q(Q[0]), .en(D[7]), .reset(RST));  // open: Qn, preset
  D_Flip_Flop d_ff_2 (.clk(not_1_out), .D(and_2_out), .Q(Q[1]), .en(D[7]), .reset(RST));  // open: Qn, preset
  D_Flip_Flop d_ff_3 (.clk(not_1_out), .D(and_3_out), .Q(Q[2]), .en(D[7]), .reset(RST));  // open: Qn, preset
  D_Flip_Flop d_ff_4 (.clk(not_1_out), .D(and_4_out), .Q(Q[3]), .en(D[7]), .reset(RST));  // open: Qn, preset
  D_Flip_Flop d_ff_5 (.clk(not_1_out), .D(and_5_out), .Q(Q[4]), .en(D[7]), .reset(RST));  // open: Qn, preset
  D_Flip_Flop d_ff_6 (.D(and_6_out), .Q(Q[5]), .en(D[7]), .reset(RST));  // open: clk, Qn, preset
  D_Flip_Flop d_ff_7 (.clk(not_1_out), .D(and_7_out), .Q(Q[6]), .en(D[7]), .reset(RST));  // open: Qn, preset
  D_Flip_Flop d_ff_8 (.clk(not_1_out), .D(and_8_out), .Q(Q[7]), .en(D[7]), .reset(RST));  // open: Qn, preset

  // Other names for the same wires on the sheet: D[6] = D[7]; EN = D[7]
endmodule
