// Logisim project hw4part2.circ as structural Verilog: 2 circuits, main circuit One-Hot State Machine
module Tester (
  input  G
);

  wire Clock_out, one_hot_state_machine_1_w, one_hot_state_machine_1_x, one_hot_state_machine_1_y,
       one_hot_state_machine_1_z, Reset_out;

  One_Hot_State_Machine one_hot_state_machine_1 (
    .W(one_hot_state_machine_1_w), .Clock(Clock_out), .Reset(Reset_out), .G(G),
    .X(one_hot_state_machine_1_x), .Y(one_hot_state_machine_1_y), .Z(one_hot_state_machine_1_z));
  Clock Clock (.out(Clock_out));
  LED W (.in(one_hot_state_machine_1_w));
  LED X (.in(one_hot_state_machine_1_x));
  LED Y (.in(one_hot_state_machine_1_y));
  LED Z (.in(one_hot_state_machine_1_z));
  Button Reset (.out(Reset_out));

  // Notes on the sheet:
  //   You can use this to test your circuit.
endmodule

module One_Hot_State_Machine (
  input  G,
  input  Clock,
  input  Reset,
  output W,
  output X,
  output Y,
  output Z
);

  wire and_1_out, and_3_out, not_1_out, not_2_out, or_1_out, or_5_out, Out1, Out2, Out3, Out4, Out5, Out6,
       S1_out, S3_out, S5_out, X1;
  wire [6:0] and_2_out;

  not not_1 (not_1_out, G);
  not not_2 (not_2_out, G);
  and S5 (S5_out, G, Out3);
  and and_1 (and_1_out, G, Out6);
  or or_1 (or_1_out, not_1_out, Out6);
  buf S1 (S1_out, G);  // AND_Gate
  and S2 (and_2_out[2], ~G, ~Out3, ~Out6, Out1);  // AND_Gate
  and S3 (S3_out, not_2_out, Out3);
  and S4 (and_2_out[4], G, ~Out4, Out1);  // AND_Gate
  or or_2 (and_2_out[5], Out4, S5_out);
  or or_3 (and_2_out[6], and_1_out, Out5);
  and and_2 (and_2_out[0], or_1_out, ~Out4, ~and_2_out[2], ~Out3, ~and_2_out[3], ~and_2_out[6]);  // AND_Gate
  and and_3 (and_3_out, Out3, ~G);  // AND_Gate
  and and_4 (and_2_out[1], ~and_2_out[5], ~and_2_out[6], S1_out);  // AND_Gate
  or or_4 (and_2_out[3], or_5_out, and_3_out);
  or or_5 (or_5_out, S3_out, Out2);
  Register #(.width(7)) register_1 (
    .D(and_2_out), .Q({Out6, Out5, Out4, Out3, Out2, Out1, X1}), .clk(Clock), .clr(Reset));  // open: en
  or or_6 (X, X1, Out3);
  or or_7 (Y, Out3, Out5, Out6);
  or or_8 (Z, Out2, Out4, Out5);
  or or_9 (W, Out2, Out3, Out6);

  // Other names for the same wires on the sheet: W1 = Out2; Z1 = Out2; W2 = Out3; X2 = Out3; Y1 = Out3; Z2 = Out4;
  //   Y2 = Out5; Z3 = Out5; W3 = Out6; Y3 = Out6; CLK = Clock; RST = Reset

  // Notes on the sheet:
  //   My name is
  //   Tuan Nguyen
  //   and this is my pretty one-hot state machine!
endmodule
