// Logisim project timedlab1.circ as structural Verilog: 2 circuits, main circuit main
module main (
  input  RST,
  input  A
);

  wire CLK_out, statemachine_1_w, statemachine_1_x, statemachine_1_y, statemachine_1_z;

  Clock CLK (.out(CLK_out));
  LED W (.in(statemachine_1_w));
  LED Y (.in(statemachine_1_y));
  LED X (.in(statemachine_1_x));
  statemachine statemachine_1 (
    .CLK(CLK_out), .RST(RST), .A(A), .W(statemachine_1_w), .X(statemachine_1_x), .Y(statemachine_1_y),
    .Z(statemachine_1_z));
  LED Z (.in(statemachine_1_z));
endmodule

module statemachine (
  input  CLK,
  input  RST,
  input  A,
  output W,
  output X,
  output Y,
  output Z
);

  wire and_2_out, or_1_out, or_2_out, S1, S2_2_out, S2_out, S3_2_out, S3_3_out, S3_4_out, S3_out, So;
  wire [4:0] and_5_out;

  and and_1 (and_5_out[1], So, ~X, ~Y, ~Z);  // AND_Gate
  and S2 (S2_out, S1, A);
  or or_1 (or_1_out, S2_out, S2_2_out);
  and S2_2 (S2_2_out, A, X);
  and S3 (S3_out, S1, ~A);  // AND_Gate
  and S3_2 (S3_2_out, Y, ~A);  // AND_Gate
  and S3_3 (S3_3_out, X, ~A);  // AND_Gate
  and S3_4 (S3_4_out, Y, A);
  and and_2 (and_2_out, ~So, ~S1, ~Y, ~X, ~and_5_out[1]);  // AND_Gate
  buf and_3 (and_5_out[2], or_1_out);  // AND_Gate
  buf and_4 (and_5_out[3], or_2_out);  // AND_Gate
  or or_2 (or_2_out, S3_out, S3_2_out);
  or or_3 (and_5_out[4], S3_3_out, S3_4_out);
  buf and_5 (and_5_out[0], and_2_out);  // AND_Gate
  Register #(.width(5)) register_1 (.D(and_5_out), .Q({Z, Y, X, S1, So}), .clk(CLK), .clr(RST));  // open: en
  or or_4 (W, Z, S1);

  // Other names for the same wires on the sheet: S2 = X; S3 = Y; S4 = Z

  // Notes on the sheet:
  //   Hello! My name is 
  //   <Tuan Nguyen>
  //   And this is my pretty state machine!
endmodule
